// Logisim project ASSIGNMENT_8.circ as structural Verilog: 1 circuit, main circuit main
module main (
  input  [3:0] Parallel_Input_3_0,
  input  CLK,
  input  RESET,
  input  PC_ENABLE,
  input  PC_LOAD,
  output [3:0] PC_Output_3_0
);

  wire LOAD_OR_INCREMENT_p3, PC_PLUS_1_p3;

  // Incrementer #(.width(4)) PC_PLUS_1: pin names not known; wires that end beside it: PC_LOAD, PC_Output_3_0, PC_PLUS_1_p3
  // Multiplexer #(.select(1), .width(4), .enable("false")) LOAD_OR_INCREMENT: pin names not known; wires that end beside it: Parallel_Input_3_0, PC_PLUS_1_p3, LOAD_OR_INCREMENT_p3
  // Register #(.width(4), .enable("true"), .reset("true"), .trigger("rising")) PC_REGISTER: pin names not known; wires that end beside it: RESET, PC_ENABLE
endmodule
