// Logisim project ASSIGNMNET_7.circ as structural Verilog: 1 circuit, main circuit main
module main (
  input  CLK,
  input  RESET,
  input  S_entry,
  input  L_top,
  input  S_exit,
  input  S_obs,
  input  L_bot,
  output M_open,
  output M_close,
  output LED_G,
  output LED_R,
  output Q1,
  output Q0
);

  wire and_1_p3, and_2_p3, and_3_p3, and_4_p3, and_5_p3, and_6_p4, or_1_p4, or_2_p4;

  not not_1 (RESET, RESET);
  // AND_Gate and_1: pin names not known; wires that end beside it: Q0, S_entry, and_1_p3
  // AND_Gate and_2: pin names not known; wires that end beside it: Q0, L_top, and_2_p3
  // AND_Gate and_3: pin names not known; wires that end beside it: Q0, S_exit, and_3_p3
  // AND_Gate and_4: pin names not known; wires that end beside it: Q0, S_exit, and_4_p3
  // AND_Gate and_5: pin names not known; wires that end beside it: Q0, S_obs, and_5_p3
  // AND_Gate and_6: pin names not known; wires that end beside it: Q0, L_bot, RESET, and_6_p4
  // OR_Gate or_1: pin names not known; wires that end beside it: and_1_p3, and_3_p3, and_2_p3, or_1_p4
  // NOT_Gate not_2: pin names not known
  // OR_Gate or_2: pin names not known; wires that end beside it: and_4_p3, and_6_p4, and_5_p3, or_2_p4
  // NOT_Gate not_3 is placed but not wired
  // D_Flip_Flop #(.trigger("rising")) DFF1__Q1: pin names not known; wires that end beside it: or_1_p4, CLK, Q0
  // D_Flip_Flop #(.trigger("rising")) DFF0__Q0: pin names not known; wires that end beside it: or_2_p4, CLK, Q0
  // AND_Gate and_7: pin names not known; wires that end beside it: Q0, Q0, M_open
  // AND_Gate and_8: pin names not known; wires that end beside it: Q0, Q0, M_close
  // AND_Gate and_9: pin names not known; wires that end beside it: LED_G
  // AND_Gate and_10: pin names not known; wires that end beside it: Q0, Q0, LED_R

  assign Q1 = Q0;
endmodule
