// Logisim project ASSIGNMNET_9.circ as structural Verilog: 1 circuit, main circuit main
module main (
  input  Input_A,
  input  Input_B,
  output Output_Y
);

  wire NOT_B_p2;

  // NOT_Gate NOT_B: pin names not known; wires that end beside it: Input_B, NOT_B_p2
  // AND_Gate A_AND_NOT_B is placed but not wired
endmodule
